// Logisim project OLA.circ as structural Verilog
module Sumador_1bit (
  input  Acarreo_in,
  input  A,
  input  B,
  output Suma,
  output Acarreo_out
);

  wire and_1_out, and_2_out, xor_1_out;

  and and_1 (and_1_out, A, B);
  or or_1 (Acarreo_out, and_1_out, and_2_out);
  xor xor_1 (xor_1_out, A, B);
  and and_2 (and_2_out, xor_1_out, Acarreo_in);
  xor xor_2 (Suma, Acarreo_in, xor_1_out);
endmodule

module S_R4_BITS (
  input  A3,
  input  B3,
  input  A2,
  input  B2,
  input  A1,
  input  B1,
  input  A0,
  input  A,
  input  in_9,
  output X,
  output out_11,
  output out_12,
  output out_13,
  output out_14
);

  wire sumador_1bit_2_acarreo_out, sumador_1bit_3_acarreo_out, sumador_1bit_4_acarreo_out, xor_1_out,
       xor_2_out, xor_3_out, xor_4_out;

  xor xor_1 (xor_1_out, in_9, A3);
  Sumador_1bit sumador_1bit_1 (
    .A(xor_1_out), .B(B3), .Acarreo_in(sumador_1bit_2_acarreo_out), .Acarreo_out(X), .Suma(out_11));
  xor xor_2 (xor_2_out, in_9, A2);
  Sumador_1bit sumador_1bit_2 (
    .A(xor_2_out), .B(B2), .Acarreo_in(sumador_1bit_3_acarreo_out), .Acarreo_out(sumador_1bit_2_acarreo_out),
    .Suma(out_12));
  xor xor_3 (xor_3_out, in_9, A1);
  Sumador_1bit sumador_1bit_3 (
    .A(xor_3_out), .B(B1), .Acarreo_in(sumador_1bit_4_acarreo_out), .Acarreo_out(sumador_1bit_3_acarreo_out),
    .Suma(out_13));
  xor xor_4 (xor_4_out, in_9, A0);
  Sumador_1bit sumador_1bit_4 (
    .A(xor_4_out), .B(A), .Acarreo_in(in_9), .Acarreo_out(sumador_1bit_4_acarreo_out), .Suma(out_14));
endmodule

module Sumador_Seleccion_8bits (
  input  A,
  input  A_2,
  input  A_3,
  input  A_4,
  input  A_5,
  input  A_6,
  input  A_7,
  input  A_8,
  input  A_9,
  input  A_10,
  input  A_11,
  input  A_12,
  input  A_13,
  input  A_14,
  input  A_15,
  input  A_16,
  input  in_17
);

  S_R4_BITS Sumador1 (
    .A3(A_9), .B3(A_10), .A2(A_11), .B2(A_12), .A1(A_13), .B1(A_14), .A0(A_15), .A(A_16));  // open: in_9, X, out_11, out_12, out_13, out_14
  S_R4_BITS Sumador2 (
    .A3(A), .B3(A_2), .A2(A_3), .B2(A_4), .A1(A_5), .B1(A_6), .A0(A_7), .A(A_8));  // open: in_9, X, out_11, out_12, out_13, out_14
endmodule

module Alu_1_bit (
  input  Acarreo_In,
  input  INVA,
  input  A,
  input  ENA,
  input  B,
  input  ENB,
  input  F0,
  input  F1,
  output Salida,
  output AcarreoSalida
);

  wire and_1_out, and_2_out, and_3_out, and_4_out, and_5_out, and_6_out, and_7_out, and_8_out, and_9_out,
       and_10_out, and_11_out, and_12_out, and_13_out, not_1_out, not_2_out, not_3_out, not_4_out, not_5_out,
       or_1_out, xor_1_out, xor_2_out, xor_3_out;

  not not_1 (not_1_out, F0);
  and and_1 (and_1_out, A, ENA);
  and and_2 (and_2_out, B, ENB);
  not not_2 (not_2_out, F1);
  not not_3 (not_3_out, F0);
  not not_4 (not_4_out, F1);
  xor xor_1 (xor_1_out, INVA, and_1_out);
  and and_3 (and_3_out, not_1_out, not_2_out);
  and and_4 (and_4_out, not_3_out, F1);
  and and_5 (and_5_out, F0, not_4_out);
  and and_6 (and_6_out, F0, F1);
  not not_5 (not_5_out, and_2_out);
  and and_7 (and_7_out, xor_1_out, and_2_out);
  or or_1 (or_1_out, xor_1_out, and_2_out);
  and and_8 (and_8_out, and_7_out, and_3_out);
  and and_9 (and_9_out, or_1_out, and_4_out);
  and and_10 (and_10_out, not_5_out, and_5_out);
  and and_11 (and_11_out, and_6_out, xor_1_out, and_2_out);
  xor xor_2 (xor_2_out, and_2_out, xor_1_out);
  or or_2 (AcarreoSalida, and_11_out, and_12_out);
  and and_12 (and_12_out, and_6_out, xor_2_out, Acarreo_In);
  xor xor_3 (xor_3_out, Acarreo_In, xor_2_out);
  and and_13 (and_13_out, xor_3_out, and_6_out);
  or or_3 (Salida, and_8_out, and_9_out, and_10_out, and_13_out);
endmodule

module Alu_8_bits (
  input  [7:0] A,
  input  [7:0] B,
  input  F0,
  input  Acarreo_IN,
  input  ENA,
  input  ENB,
  input  INVA,
  input  F1,
  input  AcarreoSalida,
  input  [7:0] Salida
);

  wire alu_1_bit_1_p10, alu_1_bit_2_p10, alu_1_bit_3_p10, alu_1_bit_4_p10, alu_1_bit_5_p10, alu_1_bit_6_p10,
       alu_1_bit_7_p10;

  // Alu_1_bit alu_1_bit_1: pin names not known; wires that end beside it: F1, F0, ENB, B[7], AcarreoSalida, ENA, Salida[7], A[7], INVA, alu_1_bit_1_p10
  // Alu_1_bit alu_1_bit_2: pin names not known; wires that end beside it: F1, F0, ENB, B[6], alu_1_bit_1_p10, ENA, Salida[6], A[6], INVA, alu_1_bit_2_p10
  // Alu_1_bit alu_1_bit_3: pin names not known; wires that end beside it: F1, F0, ENB, B[5], alu_1_bit_2_p10, ENA, Salida[5], A[5], INVA, alu_1_bit_3_p10
  // Alu_1_bit alu_1_bit_4: pin names not known; wires that end beside it: F1, F0, ENB, B[4], alu_1_bit_3_p10, ENA, Salida[4], A[4], INVA, alu_1_bit_4_p10
  // Alu_1_bit alu_1_bit_5: pin names not known; wires that end beside it: F1, F0, ENB, B[3], alu_1_bit_4_p10, ENA, Salida[3], A[3], INVA, alu_1_bit_5_p10
  // Alu_1_bit alu_1_bit_6: pin names not known; wires that end beside it: F1, F0, ENB, B[2], alu_1_bit_5_p10, ENA, Salida[2], A[2], INVA, alu_1_bit_6_p10
  // Alu_1_bit alu_1_bit_7: pin names not known; wires that end beside it: F1, F0, ENB, B[1], alu_1_bit_6_p10, ENA, Salida[1], A[1], INVA, alu_1_bit_7_p10
  Alu_1_bit alu_1_bit_8 (
    .INVA(INVA), .A(A[0]), .ENA(ENA), .B(B[0]), .ENB(ENB), .F0(F0), .F1(F1), .Acarreo_In(Acarreo_IN),
    .Salida(Salida[0]), .AcarreoSalida(alu_1_bit_7_p10));
endmodule
