// Logisim project tp6.circ as structural Verilog
module SR_LATCH (
  input  in_1,
  input  in_2,
  input  in_3,
  input  in_4,
  input  in_5,
  input  in_6,
  output out_7,
  output out_8,
  output out_9,
  output out_10
);

  wire and_1_out, and_2_out, nand_1_out, nand_2_out;

  and and_1 (and_1_out, in_1, in_2);
  and and_2 (and_2_out, in_2, in_3);
  nand nand_1 (nand_1_out, in_4, in_5);
  nand nand_2 (nand_2_out, in_5, in_6);
  nor nor_1 (out_7, and_1_out, out_8);
  nor nor_2 (out_8, out_7, and_2_out);
  nand nand_3 (out_9, nand_1_out, out_10);
  nand nand_4 (out_10, out_9, nand_2_out);
endmodule

module D_LATCH (
  input  in_1,
  input  in_2,
  output out_3,
  output out_4
);

  wire nand_1_out, nand_2_out, not_1_out;

  not not_1 (not_1_out, in_1);
  nand nand_1 (nand_1_out, in_1, in_2);
  nand nand_2 (nand_2_out, in_2, not_1_out);
  nand nand_3 (out_3, nand_1_out, out_4);
  nand nand_4 (out_4, out_3, nand_2_out);
endmodule

module JK_LATCH (
  input  in_1,
  input  in_2,
  input  in_3,
  output out_4,
  output out_5
);

  wire nand_1_out, nand_2_out;

  nand nand_1 (nand_1_out, out_5, in_1, in_2);
  nand nand_2 (nand_2_out, in_2, in_3, out_4);
  nand nand_3 (out_4, nand_1_out, out_5);
  nand nand_4 (out_5, out_4, nand_2_out);
endmodule

module T_LATCH (
  input  in_1,
  input  in_2,
  output out_3,
  output out_4
);

  wire nand_1_out, nand_2_out;

  nand nand_1 (nand_1_out, out_4, in_1, in_2);
  nand nand_2 (nand_2_out, in_2, in_1, out_3);
  nand nand_3 (out_3, nand_1_out, out_4);
  nand nand_4 (out_4, out_3, nand_2_out);
endmodule

module FLIP_FLOP_D (
  input  in_1,
  input  in_2,
  output out_3,
  output out_4
);

  wire d_latch_1_out_3, not_1_out;

  not not_1 (not_1_out, in_2);
  D_LATCH d_latch_1 (.in_1(in_1), .in_2(not_1_out), .out_3(d_latch_1_out_3));  // open: out_4
  D_LATCH d_latch_2 (.in_1(d_latch_1_out_3), .in_2(in_2), .out_3(out_3), .out_4(out_4));
endmodule

module Registro_Parelelo (
  input  [3:0] in_1,
  input  in_2,
  output out_3,
  output [3:0] out_4
);

  FLIP_FLOP_D flip_flop_d_1 (.in_1(in_2), .in_2(in_1[3]), .out_3(out_4[3]));  // open: out_4
  FLIP_FLOP_D flip_flop_d_2 (.in_1(in_2), .in_2(in_1[2]), .out_3(out_4[2]));  // open: out_4
  FLIP_FLOP_D flip_flop_d_3 (.in_1(in_2), .in_2(in_1[1]), .out_3(out_4[1]));  // open: out_4
  FLIP_FLOP_D flip_flop_d_4 (.in_1(in_2), .in_2(in_1[0]), .out_3(out_3));  // open: out_4

  assign out_4[0] = out_3;
endmodule

module Registro_Desplazador (
  input  in_1,
  input  in_2,
  output out_3,
  output [3:0] out_4
);

  FLIP_FLOP_D flip_flop_d_1 (.in_1(in_1), .in_2(in_2), .out_3(out_4[3]));  // open: out_4
  FLIP_FLOP_D flip_flop_d_2 (.in_1(in_1), .in_2(out_4[3]), .out_3(out_4[2]));  // open: out_4
  FLIP_FLOP_D flip_flop_d_3 (.in_1(in_1), .in_2(out_4[2]), .out_3(out_4[1]));  // open: out_4
  FLIP_FLOP_D flip_flop_d_4 (.in_1(in_1), .in_2(out_4[1]), .out_3(out_3));  // open: out_4

  assign out_4[0] = out_3;
endmodule
